// Logisim project Keypad.circ as structural Verilog: 2 circuits, main circuit main
module KeyPad (
  input  _0,
  input  _1,
  input  _2,
  input  _3,
  input  _4,
  input  _5,
  input  _6,
  input  _7,
  input  _8,
  input  _9,
  input  Clock,
  output [7:0] Output
);

  wire Active_out, and_1_out, not_1_out, not_2_out, not_3_out, not_4_out, or_1_out, or_2_out, or_3_out,
       or_4_out;

  or Active (Active_out, _9, _8, _7, _6, _5, _4, _3, _2, _1, _0);
  or or_1 (or_1_out, _1, _3, _5, _7, _9);
  not not_1 (not_1_out, or_1_out);
  and and_1 (and_1_out, Active_out, Clock);
  S_R_Flip_Flop s_r_ff_1 (.S(or_1_out), .clk(and_1_out), .R(not_1_out), .Q(Output[0]));  // open: Qn, preset, reset, en
  or or_2 (or_2_out, _2, _3, _6, _7);
  S_R_Flip_Flop s_r_ff_2 (.S(or_2_out), .clk(and_1_out), .R(not_2_out), .Q(Output[1]));  // open: Qn, preset, reset, en
  not not_2 (not_2_out, or_2_out);
  or or_3 (or_3_out, _4, _5, _6, _7);
  not not_3 (not_3_out, or_3_out);
  S_R_Flip_Flop s_r_ff_3 (.S(or_3_out), .clk(and_1_out), .R(not_3_out), .Q(Output[2]));  // open: Qn, preset, reset, en
  or or_4 (or_4_out, _8, _9);
  S_R_Flip_Flop s_r_ff_4 (.S(or_4_out), .clk(and_1_out), .R(not_4_out), .Q(Output[3]));  // open: Qn, preset, reset, en
  not not_4 (not_4_out, or_4_out);

  assign Output[7:4] = 4'b0000;
endmodule

module main (
  input  _0,
  input  _1,
  input  _2,
  input  _3,
  input  _4,
  input  _5,
  input  _6,
  input  _7,
  input  _8,
  input  _9,
  output [7:0] out_11
);

  wire clock_1_out;

  KeyPad keypad_1 (
    ._0(_0), ._1(_1), ._2(_2), ._3(_3), ._4(_4), ._5(_5), ._6(_6), ._7(_7), ._8(_8), ._9(_9),
    .Clock(clock_1_out), .Output(out_11));
  Clock clock_1 (.out(clock_1_out));

  // Notes on the sheet:
  //   Demo to show it works as a box
endmodule
