// Logisim project MAREvo.circ as structural Verilog: 2 circuits, main circuit MAR
module MAR (
  input  [3:0] InAdr,
  input  InOn,
  input  OutOn,
  input  Clock,
  output [3:0] OutAdr,
  output [3:0] Contents
);

  wire and_1_out, not_1_out, not_2_out, not_3_out, not_4_out;

  and and_1 (and_1_out, InOn, Clock);
  S_R_Flip_Flop s_r_ff_1 (.S(InAdr[0]), .R(not_1_out), .clk(and_1_out), .Q(Contents[0]));  // open: reset, Qn, preset
  not not_1 (not_1_out, InAdr[0]);
  S_R_Flip_Flop s_r_ff_2 (.S(InAdr[1]), .R(not_2_out), .clk(and_1_out), .Q(Contents[1]));  // open: reset, Qn, preset
  not not_2 (not_2_out, InAdr[1]);
  S_R_Flip_Flop s_r_ff_3 (.S(InAdr[2]), .R(not_3_out), .clk(and_1_out), .Q(Contents[2]));  // open: reset, Qn, preset
  not not_3 (not_3_out, InAdr[2]);
  S_R_Flip_Flop s_r_ff_4 (.S(InAdr[3]), .R(not_4_out), .clk(and_1_out), .Q(Contents[3]));  // open: reset, Qn, preset
  not not_4 (not_4_out, InAdr[3]);
  and and_2 (OutAdr[0], Contents[0], OutOn);
  and and_3 (OutAdr[1], Contents[1], OutOn);
  and and_4 (OutAdr[2], Contents[2], OutOn);
  and and_5 (OutAdr[3], Contents[3], OutOn);
endmodule

module main (
  input  [7:0] in_1,
  input  in_2,
  input  in_3,
  output [7:0] out_4,
  output [7:0] out_5
);

  wire clock_1_out;

  Clock clock_1 (.out(clock_1_out));
  // MAR mar_1: pin names not known; wires that end beside it: out_5, in_2, clock_1_out, out_4, in_1, in_3
endmodule
