// Logisim project Small_Components.circ as structural Verilog
module PC_INC (
  input  INC
);

  wire clock_1_out;
  wire [7:0] inc_1_out_3, PC_byte_out;

  INC inc_1 (.PLUS_1(INC), .in_2(PC_byte_out), .out_3(inc_1_out_3));
  Clock clock_1 (.out(clock_1_out));
  DATA_BYTE PC (.Byte_In(inc_1_out_3), .Byte_Out(PC_byte_out), .CLK(clock_1_out));
  // Probe on PC_byte_out
endmodule

module Half_Adder (
  input  A,
  input  B,
  output R,
  output C_Out
);

  wire or_1_out;

  and and_1 (C_Out, A, B);
  or or_1 (or_1_out, A, B);
  and and_2 (R, ~C_Out, or_1_out);  // AND_Gate
endmodule

module Full_Adder (
  input  A,
  input  B,
  input  C_In,
  output R,
  output C_Out
);

  wire A_B_out, A_C_out, and_1_out, and_2_out, and_3_out, B_C_out, or_1_out;

  and A_B (A_B_out, A, B);
  and A_C (A_C_out, A, C_In);
  and B_C (B_C_out, B, C_In);
  and and_1 (and_1_out, A, B, C_In);
  or or_1 (or_1_out, A, B, C_In);
  and and_2 (and_2_out, ~A_B_out, ~A_C_out, ~B_C_out);  // AND_Gate
  and and_3 (and_3_out, or_1_out, and_2_out);
  or or_2 (C_Out, A_B_out, A_C_out, B_C_out);
  or or_3 (R, and_1_out, and_3_out);
endmodule

module DATA_BYTE (
  input  [7:0] Byte_In,
  input  CLK,
  output [7:0] Byte_Out
);

  wire undriven;

  D_Flip_Flop L_0 (.D(Byte_In[0]), .clk(CLK), .Q(Byte_Out[0]));  // open: Qn, preset, reset
  D_Flip_Flop L_1 (.D(Byte_In[1]), .clk(CLK), .Q(Byte_Out[1]), .reset(undriven));  // open: Qn, preset
  D_Flip_Flop L_2 (.D(Byte_In[2]), .clk(CLK), .Q(Byte_Out[2]), .preset(undriven));  // open: Qn, reset
  D_Flip_Flop L_3 (.D(Byte_In[3]), .clk(CLK), .Q(Byte_Out[3]));  // open: Qn, preset, reset
  D_Flip_Flop L_4 (.D(Byte_In[4]), .clk(CLK), .Q(Byte_Out[4]));  // open: Qn, preset, reset
  D_Flip_Flop L_5 (.D(Byte_In[5]), .clk(CLK), .Q(Byte_Out[5]));  // open: Qn, preset, reset
  D_Flip_Flop L_6 (.D(Byte_In[6]), .clk(CLK), .Q(Byte_Out[6]));  // open: Qn, preset, reset
  D_Flip_Flop L_7 (.D(Byte_In[7]), .clk(CLK), .Q(Byte_Out[7]));  // open: Qn, preset, reset
endmodule

module INC (
  input  PLUS_1,
  input  [7:0] in_2,
  output [7:0] out_3
);

  wire half_adder_1_c_out, half_adder_2_c_out, half_adder_3_c_out, half_adder_4_c_out, half_adder_5_c_out,
       half_adder_6_c_out, half_adder_7_c_out;

  Half_Adder half_adder_1 (.A(in_2[0]), .B(PLUS_1), .R(out_3[0]), .C_Out(half_adder_1_c_out));
  Half_Adder half_adder_2 (.A(in_2[1]), .B(half_adder_1_c_out), .R(out_3[1]), .C_Out(half_adder_2_c_out));
  Half_Adder half_adder_3 (.A(in_2[2]), .B(half_adder_2_c_out), .R(out_3[2]), .C_Out(half_adder_3_c_out));
  Half_Adder half_adder_4 (.A(in_2[3]), .B(half_adder_3_c_out), .R(out_3[3]), .C_Out(half_adder_4_c_out));
  Half_Adder half_adder_5 (.A(in_2[4]), .B(half_adder_4_c_out), .R(out_3[4]), .C_Out(half_adder_5_c_out));
  Half_Adder half_adder_6 (.A(in_2[5]), .B(half_adder_5_c_out), .R(out_3[5]), .C_Out(half_adder_6_c_out));
  Half_Adder half_adder_7 (.A(in_2[6]), .B(half_adder_6_c_out), .R(out_3[6]), .C_Out(half_adder_7_c_out));
  Half_Adder half_adder_8 (.A(in_2[7]), .B(half_adder_7_c_out), .R(out_3[7]));  // open: C_Out
endmodule
